// Logisim project Task5.circ as structural Verilog: 1 circuit, main circuit main
module main (
  input  c,
  input  x,
  output [3:0] Y1Y2
);

  wire and_1_out, t_ff_1_q, t_ff_2_qn;

  and and_1 (and_1_out, t_ff_2_qn, x);
  T_Flip_Flop t_ff_1 (.clk(c), .T(and_1_out), .Q(t_ff_1_q));  // open: Qn, preset, reset
  T_Flip_Flop t_ff_2 (.clk(c), .T(x), .Q(Y1Y2[3]), .Qn(t_ff_2_qn));  // open: preset, reset
  and and_2 (Y1Y2[0], t_ff_1_q, t_ff_2_qn);
  and and_3 (Y1Y2[2], t_ff_1_q, Y1Y2[3]);

  assign Y1Y2[1] = 1'b0;
endmodule
